// Logisim project cell-machine-4+8.circ as structural Verilog: 2 circuits, main circuit Test
module CellMachine_4_8 (
  input  CLK,
  input  RESET,
  input  CLEAR_RAM,
  input  [11:0] IO_RDATA,
  output [7:0] IO_PORT,
  output [11:0] IO_WDATA,
  output IO_RE,
  output IO_WE
);

  wire ABS_TAKEN, and_5_out, and_6_out, and_7_out, and_8_out, and_9_out, comparator_1_eq, EXEC, FETCH,
       IS_ABS_JUMP, IS_ABS_NONZERO, IS_ABS_ZERO, IS_ASSIGN, IS_INDIRECT, IS_INPUT, IS_LEFT, IS_MINUS,
       IS_OUTPUT, IS_PLUS, IS_REL_JUMP, IS_REL_NONZERO, IS_REL_ZERO, IS_RIGHT, IS_WRITE_DP, IS_WRITE_PP,
       MEM_WE, not_2_out, or_1_out, or_2_out, or_3_out, or_5_out, or_6_out, PP_CONTROL_WE, PTR_WRITE,
       REL_TAKEN;
  wire [7:0] adder_1_out, adder_3_out, bit_extender_2_out, DATA_ADDR, DP, DP_NEXT, MEM_ADDR,
       multiplexer_2_out, multiplexer_5_out, PP, PP_NEXT, PP_WRITE_DATA, subtractor_2_out;
  wire [11:0] adder_2_out, bit_extender_1_out, bit_extender_3_out, bit_extender_4_out, MEM_WDATA,
       multiplexer_1_out, POINTER_WDATA, subtractor_1_out;
  wire [11:8] IR;

  Decoder #(.select(4), .enable("false")) decoder_1 (
    .out0(IS_RIGHT), .out1(IS_LEFT), .out2(IS_PLUS), .out3(IS_MINUS), .out4(IS_ASSIGN), .out5(IS_REL_ZERO),
    .out6(IS_REL_NONZERO), .out7(IS_ABS_ZERO), .out8(IS_ABS_NONZERO), .out9(IS_REL_JUMP),
    .out10(IS_ABS_JUMP), .out11(IS_WRITE_PP), .out12(IS_WRITE_DP), .out13(IS_INDIRECT), .out14(IS_INPUT),
    .out15(IS_OUTPUT), .sel(IR));
  RAM #(.dataWidth(12), .bus("separate")) ram_1 (
    .addr(MEM_ADDR), .din(MEM_WDATA), .data(IO_WDATA), .str(MEM_WE), .sel(1'b1), .clk(CLK), .ld(1'b1),
    .clr(CLEAR_RAM));
  assign bit_extender_1_out = {{4{1'b0}}, IO_PORT};  // Bit_Extender bit_extender_1
  Adder adder_1 (.a(PP), .b(IO_PORT), .out(adder_1_out), .cin(1'b0));  // open: cout
  Register #(.width(12)) register_1 (.D(IO_WDATA), .en(FETCH), .Q({IR, IO_PORT}), .clk(CLK), .clr(RESET));
  Adder #(.width(12)) adder_2 (.a(IO_WDATA), .b(bit_extender_1_out), .out(adder_2_out), .cin(1'b0));  // open: cout
  Multiplexer #(.select(2), .width(12), .enable("false")) multiplexer_1 (
    .in0(adder_2_out), .in1(subtractor_1_out), .in2(bit_extender_1_out), .in3({12{1'b0}}),
    .out(multiplexer_1_out), .sel({IS_ASSIGN, IS_MINUS}));
  Subtractor #(.width(12)) subtractor_1 (
    .a(IO_WDATA), .b(bit_extender_1_out), .out(subtractor_1_out), .bin(1'b0));  // open: bout
  Multiplexer #(.width(8), .enable("false")) multiplexer_2 (
    .in0(adder_1_out), .in1(IO_PORT), .out(multiplexer_2_out), .sel(ABS_TAKEN));
  Bit_Extender #(.in_width(12), .out_width(8)) bit_extender_2 (.in(IO_WDATA), .out(bit_extender_2_out));
  Register #(.width(1)) register_2 (.D(FETCH), .en(1'b1), .Q(EXEC), .clk(CLK), .clr(RESET));
  Multiplexer #(.select(2), .width(12), .enable("false")) multiplexer_3 (
    .in0(multiplexer_1_out), .in1(POINTER_WDATA), .in2(IO_RDATA), .in3({12{1'b0}}), .out(MEM_WDATA),
    .sel({IS_INPUT, PTR_WRITE}));
  Multiplexer #(.width(8), .enable("false")) multiplexer_4 (
    .in0(PP_NEXT), .in1(multiplexer_5_out), .out(PP_WRITE_DATA), .sel(PP_CONTROL_WE));
  Multiplexer #(.width(8), .enable("false")) multiplexer_5 (
    .in0(multiplexer_2_out), .in1(bit_extender_2_out), .out(multiplexer_5_out), .sel(IS_INDIRECT));
  not not_1 (FETCH, EXEC);
  and and_1 (IO_RE, EXEC, IS_INPUT);
  and and_2 (IO_WE, EXEC, IS_OUTPUT);
  or or_1 (or_1_out, FETCH, PP_CONTROL_WE);
  Adder adder_3 (.a(DP), .b(IO_PORT), .out(adder_3_out), .cin(1'b0));  // open: cout
  Subtractor subtractor_2 (.a(DP), .b(IO_PORT), .out(subtractor_2_out));  // open: bin, bout
  Register register_3 (.D(PP_WRITE_DATA), .en(or_1_out), .Q(PP), .clk(CLK), .clr(RESET));
  assign bit_extender_3_out = {{4{1'b0}}, PP};  // Bit_Extender bit_extender_3
  Multiplexer #(.width(12), .enable("false")) multiplexer_6 (
    .in0(bit_extender_3_out), .in1(bit_extender_4_out), .out(POINTER_WDATA), .sel(IS_WRITE_DP));
  assign bit_extender_4_out = {{4{1'b0}}, DP};  // Bit_Extender bit_extender_4
  or or_2 (or_2_out, IS_WRITE_PP, IS_WRITE_DP, IS_INDIRECT);
  Multiplexer #(.width(8), .enable("false")) multiplexer_7 (
    .in0(DP), .in1(adder_3_out), .out(DATA_ADDR), .sel(or_2_out));
  Multiplexer #(.width(8), .enable("false")) multiplexer_8 (
    .in0(adder_3_out), .in1(subtractor_2_out), .out(DP_NEXT), .sel(IS_LEFT));
  or or_3 (or_3_out, IS_PLUS, IS_MINUS, IS_ASSIGN, PTR_WRITE, IS_INPUT);
  Adder adder_4 (.a(PP), .b(8'h1), .out(PP_NEXT), .cin(1'b0));  // open: cout
  and and_3 (MEM_WE, or_3_out, EXEC);
  Comparator #(.width(12)) comparator_1 (.a(IO_WDATA), .b({12{1'b0}}), .eq(comparator_1_eq));  // open: gt, lt
  Multiplexer #(.width(8), .enable("false")) multiplexer_9 (.in0(DATA_ADDR), .in1(PP), .out(MEM_ADDR), .sel(FETCH));
  or or_4 (PTR_WRITE, IS_WRITE_PP, IS_WRITE_DP);
  or or_5 (or_5_out, REL_TAKEN, ABS_TAKEN, IS_INDIRECT);
  not not_2 (not_2_out, comparator_1_eq);
  or or_6 (or_6_out, IS_RIGHT, IS_LEFT);
  and and_4 (PP_CONTROL_WE, or_5_out, EXEC);
  and and_5 (and_5_out, comparator_1_eq, IS_REL_ZERO);
  or or_7 (REL_TAKEN, IS_REL_JUMP, and_5_out, and_6_out);
  and and_6 (and_6_out, not_2_out, IS_REL_NONZERO);
  and and_7 (and_7_out, comparator_1_eq, IS_ABS_ZERO);
  and and_8 (and_8_out, not_2_out, IS_ABS_NONZERO);
  or or_8 (ABS_TAKEN, and_7_out, and_8_out, IS_ABS_JUMP);
  and and_9 (and_9_out, or_6_out, EXEC);
  Register register_4 (.D(DP_NEXT), .en(and_9_out), .Q(DP), .clk(CLK), .clr(RESET));

  // Other names for the same wires on the sheet: DATA[11:0] = IO_WDATA; IR[7:0] = IO_PORT; OPERAND[7:0] = IO_PORT;
  //   OPCODE[3:0] = IR
endmodule

module Test (
);

  wire CLEAR_RAM, CLK, IO_RE, IO_WE, RESET;
  wire [7:0] IO_PORT, register_2_q;
  wire [11:0] IO_WDATA, register_1_q;

  Clock u_CLK (.out(CLK));
  Button u_RESET (.out(RESET));
  Button u_CLEAR_RAM (.out(CLEAR_RAM));
  CellMachine_4_8 cellmachine_4_8_1 (
    .CLK(CLK), .RESET(RESET), .CLEAR_RAM(CLEAR_RAM), .IO_RDATA(12'h123), .IO_PORT(IO_PORT),
    .IO_WDATA(IO_WDATA), .IO_RE(IO_RE), .IO_WE(IO_WE));
  Register #(.width(12)) register_1 (.D(IO_WDATA), .en(IO_WE), .Q(register_1_q), .clk(CLK), .clr(RESET));
  // Probe on register_1_q
  // Probe on register_2_q
  Register register_2 (.D(IO_PORT), .en(IO_WE), .Q(register_2_q), .clk(CLK), .clr(RESET));
endmodule
